# Fritzing sketch 02_outdoor_weather (saved by Fritzing 1.0.4)
breadboards: 1

parts:
  Raspberry_Pi_Pico_W = Raspberry Pi Pico W
  DHT22 = DHT22 Humidity and Temperature Sensor
  BMP280 = BME280

nets:
  N1: Raspberry_Pi_Pico_W.pin_1, BMP280.SDA
  N2: Raspberry_Pi_Pico_W.pin_2, BMP280.SCL
  GND: Raspberry_Pi_Pico_W.pin_3, Raspberry_Pi_Pico_W.pin_8, Raspberry_Pi_Pico_W.pin_13, Raspberry_Pi_Pico_W.pin_18, Raspberry_Pi_Pico_W.pin_23, Raspberry_Pi_Pico_W.pin_28, Raspberry_Pi_Pico_W.pin_33, Raspberry_Pi_Pico_W.pin_38, DHT22.GND, BMP280.GND
  N3: Raspberry_Pi_Pico_W.pin_4, DHT22.DATA
  VDD: Raspberry_Pi_Pico_W.pin_36, DHT22.VDD, BMP280.VIN

custom parts:
  Raspberry Pi Pico W: Raspberry Pi Pico W. Based around the RP2040 microcontroller the Pico W is a low cost microcontroller device bringing Raspberry Pi quality, cost, and easy of use to the microcontroller space. The areas marked KEEPOUT in pcb silkscreen should not have traces running through them to avoid shorts on a soldered in module!
  BME280: Temperature Humidity Barometric presure Sensor
